# Fritzing sketch diagram (saved by Fritzing 0.9.10b)

parts:
  Part11 = Arduino Nano (Rev3.0)
  A5 = j5019
  U4 = LIPO-1000mAh [package=lipo-1000]
  Grove_Button_P2 = Grove Button (P)
  HC-3 = HC-12 Module
  Part14 = MQ-3 breakout
  A6 = Force sensitive resistor - square
  A7 = Force sensitive resistor - square
  SIM800L3 = SIM800L
  M4 = NEO-6M GPS Module [part_number=GY-GPS6MV2]
  Part17 = Passive Buzzer
  GY4 = MPU-6050 Board GY-521 [form="♀ (female)" package=THT]
  KY-2 = Keyes Relay [package=THT]
  HC-4 = HC-12 Module
  Part18 = Arduino Uno (Rev3)
  J34 = female pin header, 2 pins [form="♀ (female)"]
  J35 = female pin header, 2 pins [form="♀ (female)"]
  J38 = female pin header, 2 pins [form="♀ (female)"]
  J39 = female pin header, 2 pins [form="♀ (female)"]
  J40 = female pin header, 2 pins [form="♀ (female)"]
  J41 = female pin header, 2 pins [form="♀ (female)"]
  J43 = female pin header, 2 pins [form="♀ (female)"]
  J45 = female pin header, 2 pins [form="♀ (female)"]
  J46 = female pin header, 2 pins [form="♀ (female)"]
  M5 = NEO-6M GPS Module [part_number=GY-GPS6MV2]
  J47 = female pin header, 2 pins [form="♀ (female)"]
  R1 = Resistor [tolerance=±5% resistance=220 package="2010 [SMD]"]
  J48 = female pin header, 2 pins [form="♀ (female)"]
  R2 = Resistor [tolerance=±5% resistance=220 package="2010 [SMD]"]
  J49 = female pin header, 2 pins [form="♀ (female)"]
  J50 = female pin header, 2 pins [form="♀ (female)"]
  J51 = female pin header, 2 pins [form="♀ (female)"]
  GSM_SIM_GPSR_SMS_SIM900_SIM1 = SIM800L [package=THT]

nets:
  N1: Part11.D2, HC-3.TXD
  N2: Part11.D3, HC-3.RXD
  N3: Part11.D4, M5.Tx
  N4: Part11.D5, M5.Rx, M5.Vcc, J47.pin2
  N5: Part11.D6, SIM800L3.TXD
  N6: Part11.D7, SIM800L3.RXD
  N7: Part11.D8, Grove_Button_P2.NC
  N8: Part11.D9, Grove_Button_P2.SIG
  N9: Part11.VIN, A5.Pin_1
  N10: Part11.GND, A5.Pin_2, A5.Pin_4, A5.Pin_5, U4.-
  N11: Part11.A2, Part14.DO
  N12: Part11.A1, A7.Pin_2, R2.Pin_0
  N13: Part11.A0, A6.Pin_2, R1.Pin_0
  N14: A5.Pin_6, U4.+
  N15: Grove_Button_P2.VCC, J46.pin1
  N16: Grove_Button_P2.GND, J46.pin2
  N17: HC-3.GND, J34.pin1
  N18: HC-3.VCC, J34.pin2
  N19: Part14.VCC, J45.pin2
  N20: Part14.GND, J45.pin1
  N21: A6.Pin_1, J48.pin2
  N22: A7.Pin_1, J49.pin2
  N23: SIM800L3.NET, SIM800L3.VCC, J43.pin1
  N24: SIM800L3.GND, J43.pin2
  N25: M4.GND, J39.pin1
  N26: M4.Tx, Part18.D4
  N27: M4.Rx, Part18.D5_PWM
  N28: M4.Vcc, J39.pin2
  N29: Part17.GND, J38.pin1
  N30: Part17.S, Part18.D10_PWM/SS
  N31: Part17.NC, J38.pin2
  N32: GY4.pin1, J41.pin2
  N33: GY4.pin2, J41.pin1
  N34: GY4.pin3, Part18.A5/SCL
  N35: GY4.pin4, GY4.pin5, Part18.A4/SDA
  N36: KY-2.signal, Part18.D12/MISO
  N37: KY-2.power, J50.pin1
  N38: KY-2.ground, J50.pin2
  N39: KY-2.C, J51.pin1
  N40: KY-2.NO, J51.pin2
  N41: HC-4.SET, HC-4.TXD, Part18.D2
  N42: HC-4.RXD, Part18.D3_PWM
  N43: HC-4.GND, J35.pin1
  N44: HC-4.VCC, J35.pin2
  N45: Part18.D6_PWM, GSM_SIM_GPSR_SMS_SIM900_SIM1.SIM_TXD
  N46: Part18.D7, GSM_SIM_GPSR_SMS_SIM900_SIM1.SIM_RXD
  N47: J40.pin1, GSM_SIM_GPSR_SMS_SIM900_SIM1.GND
  N48: J40.pin2, GSM_SIM_GPSR_SMS_SIM900_SIM1.5V
  N49: M5.GND, J47.pin1
  N50: R1.Pin_1, J48.pin1
  N51: R2.Pin_1, J49.pin1

custom parts:
  j5019: This module is a small single cell lithium battery charging module which also includes a 1A step-up (boost) converter for powering a large range of applications.
  Grove Button (P): Button, Grove connector, panel mount.
  HC-12 Module: HC-12 433Mhz Module
  MQ-3 breakout: Alcohol sensor is capable of detecting alcohol (ethanol) particles on itself and gives the information in digital form back to us to manipulate with it. SKU:101251 • Voltage: 5V DC • Power: max 750mW • Measurement range: 0.04-4mg/L
  Force sensitive resistor - square: Force sensitive resistor - square.
  SIM800L: SIM800L is a miniature cellular module which allows for GPRS transmission, sending and receiving SMS and making and receiving voice calls. Low cost and small footprint and quad band frequency support make this module perfect solution for any project that require long range connectivity. After connecting power module boots up, searches for cellular network and login automatically. On board LED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
  NEO-6M GPS Module: GY-GPS6MV2 NEO-6M GPS Module Module based on U-blox NEO-6M GPS engine, incorporating regulator for 3.3-5V DC input, MS621FE-compatible rechargeable battery for backup and EEPROM for storing configuration settings. Links: NEO-6 series product information page NEO-6 Datasheet
  MPU-6050 Board GY-521: Acelerometro y Giroscopio MPU-6050 Board GY-521
  Keyes Relay: The Keyes 5V relay module is suitable for SCM development, home appliance control. It uses a 5V~12V TIL control signal which can control DC / AC signal.
